// Logisim project alu.circ as structural Verilog: 1 circuit, main circuit alu
module alu (
  input  [31:0] A,
  input  [31:0] B,
  input  [3:0] ALUSel,
  output [31:0] ALUResult
);

  wire comparator_1_lt;
  wire [4:0] bit_extender_1_out, bit_extender_2_out, bit_extender_3_out;
  wire [31:0] AddOut, AndOut, MulhOut, MulhuOut, MulOut, OrOut, SllOut, SltOut, SraOut, SrlOut, SubOut,
       XorOut;

  Adder #(.width(32)) adder_1 (.a(A), .b(B), .out(AddOut));  // open: cin, cout
  Bit_Extender #(.in_width(32), .out_width(5), .\type ("zero")) bit_extender_1 (.in(B), .out(bit_extender_1_out));
  Comparator #(.width(32)) comparator_1 (.a(A), .b(B), .lt(comparator_1_lt));  // open: gt, eq
  assign XorOut = A ^ B;  // XOR_Gate xor_1, 32 bits wide
  Bit_Extender #(.in_width(32), .out_width(5), .\type ("zero")) bit_extender_2 (.in(B), .out(bit_extender_2_out));
  assign OrOut = A | B;  // OR_Gate or_1, 32 bits wide
  assign AndOut = A & B;  // AND_Gate and_1, 32 bits wide
  Multiplier #(.mode("twosComplement"), .width(32)) multiplier_1 (.a(A), .b(B), .out(MulOut));  // open: cin, cout
  Multiplier #(.mode("twosComplement"), .width(32)) multiplier_2 (.a(A), .b(B), .cout(MulhOut));  // open: out, cin
  Multiplier #(.width(32)) multiplier_3 (.a(A), .b(B), .cout(MulhuOut));  // open: out, cin
  Subtractor #(.width(32)) subtractor_1 (.a(A), .b(B), .out(SubOut));  // open: bin, bout
  Bit_Extender #(.in_width(32), .out_width(5), .\type ("zero")) bit_extender_3 (.in(B), .out(bit_extender_3_out));
  Shifter #(.width(32)) shifter_1 (.in(A), .\dist (bit_extender_1_out), .out(SllOut));
  assign SltOut = {{31{1'b0}}, comparator_1_lt};  // Bit_Extender bit_extender_4
  Shifter #(.shift("lr"), .width(32)) shifter_2 (.in(A), .\dist (bit_extender_2_out), .out(SrlOut));
  Shifter #(.shift("ar"), .width(32)) shifter_3 (.in(A), .\dist (bit_extender_3_out), .out(SraOut));
  Multiplexer #(.select(4), .width(32)) multiplexer_1 (
    .in0(AddOut), .in1(SllOut), .in2(SltOut), .in4(XorOut), .in5(SrlOut), .in6(OrOut), .in7(AndOut),
    .in8(MulOut), .in9(MulhOut), .in11(MulhuOut), .in12(SubOut), .in13(SraOut), .in15(B), .out(ALUResult),
    .sel(ALUSel));  // open: in3, in10, in14

  // Other names for the same wires on the sheet: BselOut[31:0] = B

  // Notes on the sheet:
  //   INPUTS to your circuit
  //   ADD
  //   SLL
  //   SLT
  //   XOR
  //   SRL
  //   OR
  //   AND
  //   MUL
  //   MULH
  //   MULHU
  //   SUB
  //   SRA
  //   BSEL
  //   DON'T CHANGE THE LOCATIONS OF THE INPUTS AND OUTPUTS!
  //   OUTPUT from your circuit
endmodule
