// Logisim project control-logic.circ as structural Verilog: 1 circuit, main circuit control_logic
module control_logic (
  input  [31:0] Instruction,
  input  BrEq,
  input  BrLt,
  output PCSel,
  output RegWEn,
  output [2:0] ImmSel,
  output BrUn,
  output ASel,
  output BSel,
  output [3:0] ALUSel,
  output MemWEn,
  output [1:0] WBSel
);

  wire and_1_out, and_2_out, and_3_out, and_5_out, and_6_out, and_7_out, and_8_out, and_9_out, and_10_out,
       and_11_out, and_12_out, and_13_out, and_14_out, and_21_out, and_22_out, and_23_out, and_24_out,
       and_25_out, and_26_out, and_27_out, and_28_out, and_29_out, and_30_out, and_31_out, and_32_out,
       and_33_out, and_34_out, and_35_out, and_36_out, and_37_out, and_38_out, and_39_out, and_40_out,
       and_41_out, and_42_out, and_43_out, and_44_out, beq, bge, bgeu, blt, bltu, bne, comparator_1_eq,
       comparator_2_eq, comparator_3_eq, comparator_4_eq, comparator_5_eq, comparator_6_eq, comparator_7_eq,
       comparator_8_eq, comparator_9_eq, comparator_10_eq, comparator_11_eq, comparator_12_eq,
       comparator_13_eq, comparator_14_eq, comparator_15_eq, comparator_16_eq, comparator_17_eq,
       comparator_18_eq, comparator_20_eq, comparator_21_eq, comparator_22_eq, comparator_23_eq,
       comparator_24_eq, comparator_25_eq, comparator_26_eq, comparator_27_eq, comparator_28_eq,
       comparator_29_eq, comparator_30_eq, comparator_31_eq, comparator_32_eq, comparator_33_eq,
       comparator_34_eq, comparator_35_eq, comparator_36_eq, comparator_37_eq, comparator_38_eq,
       comparator_39_eq, comparator_40_eq, comparator_41_eq, comparator_42_eq, jal, jalr, not_1_out,
       not_2_out, not_3_out, or_1_out, or_2_out;
  wire [5:0] rominput;
  wire [15:14] rom_1_data;

  Comparator #(.width(7)) comparator_1 (.a(7'b0010011), .b(Instruction[6:0]), .eq(comparator_1_eq));  // open: gt, lt
  Comparator #(.width(7)) comparator_2 (.a(7'b0100011), .b(Instruction[6:0]), .eq(comparator_2_eq));  // open: gt, lt
  Comparator #(.width(7)) comparator_3 (.a(7'b0000011), .b(Instruction[6:0]), .eq(comparator_3_eq));  // open: gt, lt
  ROM #(.addrWidth(6), .dataWidth(16)) rom_1 (
    .addr(rominput), .data({rom_1_data, WBSel, MemWEn, ALUSel, BSel, ASel, BrUn, ImmSel, RegWEn}));
  Comparator #(.width(3)) comparator_4 (.a(Instruction[14:12]), .b(3'b000), .eq(comparator_4_eq));  // open: gt, lt
  Comparator #(.width(3)) comparator_5 (.a(Instruction[14:12]), .b(3'b111), .eq(comparator_5_eq));  // open: gt, lt
  Comparator #(.width(3)) comparator_6 (.a(Instruction[14:12]), .b(3'b110), .eq(comparator_6_eq));  // open: gt, lt
  Comparator #(.width(3)) comparator_7 (.a(Instruction[14:12]), .b(3'b100), .eq(comparator_7_eq));  // open: gt, lt
  Comparator #(.width(3)) comparator_8 (.a(Instruction[14:12]), .b(3'b001), .eq(comparator_8_eq));  // open: gt, lt
  Comparator #(.width(3)) comparator_9 (.a(Instruction[14:12]), .b(3'b101), .eq(comparator_9_eq));  // open: gt, lt
  Comparator #(.width(3)) comparator_10 (.a(Instruction[14:12]), .b(3'b010), .eq(comparator_10_eq));  // open: gt, lt
  Comparator #(.width(7)) comparator_11 (.a(Instruction[31:25]), .b({7{1'b0}}), .eq(comparator_11_eq));  // open: gt, lt
  Comparator #(.width(7)) comparator_12 (
    .a(Instruction[31:25]), .b(7'b0100000), .eq(comparator_12_eq));  // open: gt, lt
  Comparator #(.width(3)) comparator_13 (.a(3'b000), .b(Instruction[14:12]), .eq(comparator_13_eq));  // open: gt, lt
  Comparator #(.width(3)) comparator_14 (.a(3'b001), .b(Instruction[14:12]), .eq(comparator_14_eq));  // open: gt, lt
  Comparator #(.width(3)) comparator_15 (.a(3'b010), .b(Instruction[14:12]), .eq(comparator_15_eq));  // open: gt, lt
  Comparator #(.width(3)) comparator_16 (.a(3'b000), .b(Instruction[14:12]), .eq(comparator_16_eq));  // open: gt, lt
  Comparator #(.width(3)) comparator_17 (.a(3'b001), .b(Instruction[14:12]), .eq(comparator_17_eq));  // open: gt, lt
  Comparator #(.width(3)) comparator_18 (.a(3'b010), .b(Instruction[14:12]), .eq(comparator_18_eq));  // open: gt, lt
  Comparator #(.width(7)) comparator_19 (.a(7'b1101111), .b(Instruction[6:0]), .eq(jal));  // open: gt, lt
  Comparator #(.width(7)) comparator_20 (.a(7'b1100111), .b(Instruction[6:0]), .eq(comparator_20_eq));  // open: gt, lt
  Comparator #(.width(3)) comparator_21 (.a(Instruction[14:12]), .b(3'b000), .eq(comparator_21_eq));  // open: gt, lt
  Comparator #(.width(7)) comparator_22 (.a(7'b0010111), .b(Instruction[6:0]), .eq(comparator_22_eq));  // open: gt, lt
  Comparator #(.width(7)) comparator_23 (.a(7'b0110111), .b(Instruction[6:0]), .eq(comparator_23_eq));  // open: gt, lt
  and and_1 (and_1_out, comparator_1_eq, comparator_4_eq);
  and and_2 (and_2_out, comparator_1_eq, comparator_5_eq);
  and and_3 (and_3_out, comparator_1_eq, comparator_6_eq);
  Comparator #(.width(7)) comparator_24 (.a(7'b0110011), .b(Instruction[6:0]), .eq(comparator_24_eq));  // open: gt, lt
  Comparator #(.width(7)) comparator_25 (.a(7'b1100011), .b(Instruction[6:0]), .eq(comparator_25_eq));  // open: gt, lt
  and and_4 (jalr, comparator_20_eq, comparator_21_eq);
  and and_5 (and_5_out, comparator_1_eq, comparator_7_eq);
  and and_6 (and_6_out, comparator_1_eq, comparator_8_eq);
  and and_7 (and_7_out, comparator_9_eq, comparator_12_eq);
  and and_8 (and_8_out, comparator_9_eq, comparator_11_eq);
  and and_9 (and_9_out, comparator_1_eq, comparator_10_eq);
  Comparator #(.width(3)) comparator_26 (.a(Instruction[14:12]), .b(3'b000), .eq(comparator_26_eq));  // open: gt, lt
  Comparator #(.width(3)) comparator_27 (.a(Instruction[14:12]), .b(3'b001), .eq(comparator_27_eq));  // open: gt, lt
  Comparator #(.width(3)) comparator_28 (.a(Instruction[14:12]), .b(3'b010), .eq(comparator_28_eq));  // open: gt, lt
  Comparator #(.width(3)) comparator_29 (.a(Instruction[14:12]), .b(3'b011), .eq(comparator_29_eq));  // open: gt, lt
  Comparator #(.width(3)) comparator_30 (.a(Instruction[14:12]), .b(3'b100), .eq(comparator_30_eq));  // open: gt, lt
  Comparator #(.width(3)) comparator_31 (.a(Instruction[14:12]), .b(3'b101), .eq(comparator_31_eq));  // open: gt, lt
  Comparator #(.width(3)) comparator_32 (.a(Instruction[14:12]), .b(3'b110), .eq(comparator_32_eq));  // open: gt, lt
  Comparator #(.width(3)) comparator_33 (.a(Instruction[14:12]), .b(3'b111), .eq(comparator_33_eq));  // open: gt, lt
  Comparator #(.width(7)) comparator_34 (.a(Instruction[31:25]), .b({7{1'b0}}), .eq(comparator_34_eq));  // open: gt, lt
  Comparator #(.width(7)) comparator_35 (
    .a(Instruction[31:25]), .b(7'b0100000), .eq(comparator_35_eq));  // open: gt, lt
  Comparator #(.width(7)) comparator_36 (
    .a(Instruction[31:25]), .b(7'b0000001), .eq(comparator_36_eq));  // open: gt, lt
  Comparator #(.width(3)) comparator_37 (.a(Instruction[14:12]), .b(3'b000), .eq(comparator_37_eq));  // open: gt, lt
  Comparator #(.width(3)) comparator_38 (.a(Instruction[14:12]), .b(3'b101), .eq(comparator_38_eq));  // open: gt, lt
  Comparator #(.width(3)) comparator_39 (.a(Instruction[14:12]), .b(3'b111), .eq(comparator_39_eq));  // open: gt, lt
  Comparator #(.width(3)) comparator_40 (.a(Instruction[14:12]), .b(3'b100), .eq(comparator_40_eq));  // open: gt, lt
  Comparator #(.width(3)) comparator_41 (.a(Instruction[14:12]), .b(3'b110), .eq(comparator_41_eq));  // open: gt, lt
  Comparator #(.width(3)) comparator_42 (.a(Instruction[14:12]), .b(3'b001), .eq(comparator_42_eq));  // open: gt, lt
  and and_10 (and_10_out, comparator_2_eq, comparator_13_eq);
  and and_11 (and_11_out, comparator_2_eq, comparator_14_eq);
  and and_12 (and_12_out, comparator_2_eq, comparator_15_eq);
  and and_13 (and_13_out, comparator_1_eq, and_7_out);
  and and_14 (and_14_out, comparator_1_eq, and_8_out);
  and and_15 (beq, comparator_25_eq, comparator_37_eq);
  and and_16 (bge, comparator_25_eq, comparator_38_eq);
  and and_17 (bgeu, comparator_25_eq, comparator_39_eq);
  and and_18 (blt, comparator_25_eq, comparator_40_eq);
  and and_19 (bltu, comparator_25_eq, comparator_41_eq);
  and and_20 (bne, comparator_42_eq, comparator_25_eq);
  and and_21 (and_21_out, comparator_3_eq, comparator_16_eq);
  and and_22 (and_22_out, comparator_3_eq, comparator_17_eq);
  and and_23 (and_23_out, comparator_3_eq, comparator_18_eq);
  and and_24 (and_24_out, comparator_24_eq, comparator_31_eq);
  and and_25 (and_25_out, comparator_32_eq, comparator_24_eq);
  and and_26 (and_26_out, comparator_33_eq, comparator_24_eq);
  and and_27 (and_27_out, comparator_24_eq, comparator_26_eq);
  and and_28 (and_28_out, comparator_27_eq, comparator_24_eq);
  and and_29 (and_29_out, comparator_24_eq, comparator_28_eq);
  and and_30 (and_30_out, comparator_24_eq, comparator_29_eq);
  and and_31 (and_31_out, comparator_24_eq, comparator_30_eq);
  and and_32 (and_32_out, comparator_36_eq, and_27_out);
  and and_33 (and_33_out, and_27_out, comparator_34_eq);
  and and_34 (and_34_out, and_27_out, comparator_35_eq);
  and and_35 (and_35_out, and_28_out, comparator_34_eq);
  and and_36 (and_36_out, and_28_out, comparator_36_eq);
  and and_37 (and_37_out, and_24_out, comparator_34_eq);
  and and_38 (and_38_out, and_24_out, comparator_35_eq);
  not not_1 (not_1_out, BrLt);
  not not_2 (not_2_out, BrLt);
  not not_3 (not_3_out, BrEq);
  and and_39 (and_39_out, BrEq, beq);
  and and_40 (and_40_out, not_1_out, bge);
  and and_41 (and_41_out, not_2_out, bgeu);
  and and_42 (and_42_out, BrLt, blt);
  and and_43 (and_43_out, not_3_out, bne);
  and and_44 (and_44_out, BrLt, bltu);
  or or_1 (or_1_out, and_39_out, and_40_out, and_41_out, and_42_out, and_43_out, and_44_out);
  or or_2 (or_2_out, jal, jalr);
  or or_3 (PCSel, or_1_out, or_2_out);
  Priority_Encoder #(.select_enc(6)) priority_encoder_1 (
    .in0(and_33_out), .in1(and_32_out), .in2(and_34_out), .in3(and_35_out), .in4(and_36_out),
    .in5(and_30_out), .in6(and_29_out), .in7(and_31_out), .in8(and_37_out), .in9(and_38_out),
    .in10(and_25_out), .in11(and_26_out), .in12(and_21_out), .in13(and_22_out), .in14(and_23_out),
    .in15(and_1_out), .in16(and_6_out), .in17(and_9_out), .in18(and_5_out), .in19(and_14_out),
    .in20(and_13_out), .in21(and_3_out), .in22(and_2_out), .in23(and_10_out), .in24(and_11_out),
    .in25(and_12_out), .in26(beq), .in27(bne), .in28(blt), .in29(bge), .in30(bltu), .in31(bgeu),
    .in32(comparator_22_eq), .in33(comparator_23_eq), .in34(jal), .in35(jalr), .out(rominput));  // open: in36, in37, in38, in39, in40, in41, in42, in43, in44, in45, in46, in47, in48, in49, in50, in51, in52, in53, in54, in55, in56, in57, in58, in59, in60, in61, in62, in63, gs, en_out, en_in

  // Notes on the sheet:
  //   INPUTS to your circuit
  //   contents of rom_1 (hex, n*v repeats v):
  //   1001 1401 1601 1081 1481 1581 1101 1201 1281 1681 1301 1381 41 41 41 1041 10c1 1141 1241 12c1 16c1
  //   1341 13c1 842 842 842 4*64 74 74 1067 17e7 2069 2041
  //   ROM FOR CONTROL LOGIC
  //   DON'T CHANGE THE LOCATIONS OF THE INPUTS AND OUTPUTS!
  //   This is only if you choose to do the ROM option
  //   CONNECT
  //   WIRE
  //   TO
  //   USE
  //   ROM
  //   OUTPUT from your circuit
  //   Reminder: If using ROM, use combinational logic for PCSel
endmodule
