// Logisim project partial-load.circ as structural Verilog: 1 circuit, main circuit partial_load
module partial_load (
  input  [31:0] Instruction,
  input  [31:0] MemAddress,
  input  [31:0] DataFromMem,
  output [31:0] DataToReg
);

  wire comparator_5_eq, comparator_6_eq, comparator_7_eq, comparator_8_eq, itsa0, itsa1, itsa2, itsa3, lb,
       lh, lw;
  wire [7:0] multiplexer_1_out;
  wire [15:0] multiplexer_2_out;
  wire [31:0] bit_extender_1_out, bit_extender_2_out, multiplexer_3_out;

  Comparator #(.width(2)) comparator_1 (.a(2'b00), .b(MemAddress[1:0]), .eq(itsa0));  // open: gt, lt
  Comparator #(.width(2)) comparator_2 (.a(MemAddress[1:0]), .b(2'b01), .eq(itsa1));  // open: gt, lt
  Comparator #(.width(2)) comparator_3 (.a(MemAddress[1:0]), .b(2'b10), .eq(itsa2));  // open: gt, lt
  Comparator #(.width(2)) comparator_4 (.a(MemAddress[1:0]), .b(2'b11), .eq(itsa3));  // open: gt, lt
  Comparator #(.width(7)) comparator_5 (.a(7'b0000011), .b(Instruction[6:0]), .eq(comparator_5_eq));  // open: gt, lt
  Comparator #(.width(3)) comparator_6 (.a(3'b000), .b(Instruction[14:12]), .eq(comparator_6_eq));  // open: gt, lt
  Comparator #(.width(3)) comparator_7 (.a(3'b001), .b(Instruction[14:12]), .eq(comparator_7_eq));  // open: gt, lt
  Comparator #(.width(3)) comparator_8 (.a(3'b010), .b(Instruction[14:12]), .eq(comparator_8_eq));  // open: gt, lt
  and and_1 (lb, comparator_5_eq, comparator_6_eq);
  and and_2 (lh, comparator_5_eq, comparator_7_eq);
  and and_3 (lw, comparator_5_eq, comparator_8_eq);
  Multiplexer #(.select(2), .width(8)) multiplexer_1 (
    .in0(DataFromMem[7:0]), .in1(DataFromMem[15:8]), .in2(DataFromMem[23:16]), .in3(DataFromMem[31:24]),
    .out(multiplexer_1_out), .sel(MemAddress[1:0]));
  assign bit_extender_1_out = {{24{multiplexer_1_out[7]}}, multiplexer_1_out};  // Bit_Extender bit_extender_1
  assign bit_extender_2_out = {{16{multiplexer_2_out[15]}}, multiplexer_2_out};  // Bit_Extender bit_extender_2
  Multiplexer #(.select(2), .width(16)) multiplexer_2 (
    .in0(DataFromMem[15:0]), .in1(DataFromMem[23:8]), .in2(DataFromMem[31:16]), .out(multiplexer_2_out),
    .sel(MemAddress[1:0]));  // open: in3
  Multiplexer #(.width(32)) multiplexer_3 (
    .in0(DataFromMem), .in1(bit_extender_2_out), .out(multiplexer_3_out), .sel(lh));
  Multiplexer #(.width(32)) multiplexer_4 (
    .in0(multiplexer_3_out), .in1(bit_extender_1_out), .out(DataToReg), .sel(lb));

  // Other names for the same wires on the sheet: btm2[1:0] = MemAddress[1:0]

  // Notes on the sheet:
  //   INPUTS to your circuit
  //   DON'T CHANGE THE LOCATIONS OF THE INPUTS AND OUTPUTS!
  //   OUTPUT from your circuit
endmodule
