// Logisim project partial-store.circ as structural Verilog: 1 circuit, main circuit partial_store
module partial_store (
  input  [31:0] Instruction,
  input  [31:0] MemAddress,
  input  [31:0] DataFromReg,
  input  MemWEn,
  output [3:0] MemWriteMask,
  output [31:0] DataToMem
);

  wire and_1_out, and_2_out, and_3_out, and_4_out, and_5_out, and_6_out, comparator_1_eq, comparator_2_eq,
       comparator_3_eq, comparator_4_eq, comparator_5_eq, comparator_6_eq, comparator_7_eq, comparator_8_eq,
       not_1_out, sb, sh, sw;
  wire [15:0] bit_extender_3_out;
  wire [23:0] bit_extender_2_out;
  wire [31:0] bit_extender_1_out, bit_extender_4_out, multiplexer_1_out, multiplexer_2_out, multiplexer_3_out;

  Comparator #(.width(2)) comparator_1 (.a(MemAddress[1:0]), .b(2'b00), .eq(comparator_1_eq));  // open: gt, lt
  Comparator #(.width(2)) comparator_2 (.a(MemAddress[1:0]), .b(2'b01), .eq(comparator_2_eq));  // open: gt, lt
  Comparator #(.width(2)) comparator_3 (.a(MemAddress[1:0]), .b(2'b10), .eq(comparator_3_eq));  // open: gt, lt
  Comparator #(.width(2)) comparator_4 (.a(MemAddress[1:0]), .b(2'b11), .eq(comparator_4_eq));  // open: gt, lt
  Comparator #(.width(7)) comparator_5 (.a(7'b0100011), .b(Instruction[6:0]), .eq(comparator_5_eq));  // open: gt, lt
  Comparator #(.width(3)) comparator_6 (.a(3'b000), .b(Instruction[14:12]), .eq(comparator_6_eq));  // open: gt, lt
  Comparator #(.width(3)) comparator_7 (.a(3'b001), .b(Instruction[14:12]), .eq(comparator_7_eq));  // open: gt, lt
  Comparator #(.width(3)) comparator_8 (.a(3'b010), .b(Instruction[14:12]), .eq(comparator_8_eq));  // open: gt, lt
  and and_1 (and_1_out, sb, comparator_1_eq);
  and and_2 (and_2_out, sb, comparator_2_eq);
  and and_3 (and_3_out, sb, comparator_3_eq);
  and and_4 (and_4_out, sb, comparator_4_eq);
  and and_5 (and_5_out, sh, comparator_1_eq);
  and and_6 (and_6_out, sh, comparator_3_eq);
  assign bit_extender_1_out = {{24{1'b0}}, DataFromReg[7:0]};  // Bit_Extender bit_extender_1
  assign bit_extender_2_out = {{16{1'b0}}, DataFromReg[7:0]};  // Bit_Extender bit_extender_2
  assign bit_extender_3_out = {{8{1'b0}}, DataFromReg[7:0]};  // Bit_Extender bit_extender_3
  and and_7 (sb, comparator_5_eq, comparator_6_eq);
  and and_8 (sh, comparator_5_eq, comparator_7_eq);
  and and_9 (sw, comparator_5_eq, comparator_8_eq);
  not not_1 (not_1_out, MemWEn);
  assign bit_extender_4_out = {{16{1'b0}}, DataFromReg[15:0]};  // Bit_Extender bit_extender_4
  Bit_Extender #(.in_width(24), .out_width(32), .\type ("zero")) bit_extender_5 (.in({DataFromReg[23:8], {8{1'b0}}}));  // open: out
  Multiplexer #(.select(2), .width(32)) multiplexer_1 (
    .in0(bit_extender_1_out), .in1({bit_extender_2_out, {8{1'b0}}}), .in2({bit_extender_3_out, {16{1'b0}}}),
    .in3({DataFromReg[7:0], {24{1'b0}}}), .out(multiplexer_1_out), .sel(MemAddress[1:0]));
  Priority_Encoder #(.select_enc(4)) priority_encoder_1 (
    .in0(not_1_out), .in1(and_1_out), .in2(and_2_out), .in3(and_5_out), .in4(and_3_out), .in8(and_4_out),
    .in12(and_6_out), .in15(sw), .out(MemWriteMask));  // open: in5, in6, in7, in9, in10, in11, in13, in14, gs, en_out, en_in
  Multiplexer #(.select(2), .width(32)) multiplexer_2 (
    .in0(bit_extender_4_out), .in2({DataFromReg[15:0], {16{1'b0}}}), .out(multiplexer_2_out),
    .sel(MemAddress[1:0]));  // open: in1, in3
  Multiplexer #(.width(32)) multiplexer_3 (
    .in0(DataFromReg), .in1(multiplexer_2_out), .out(multiplexer_3_out), .sel(sh));
  Multiplexer #(.width(32)) multiplexer_4 (.in0(multiplexer_3_out), .in1(multiplexer_1_out), .out(DataToMem), .sel(sb));

  // Other names for the same wires on the sheet: btm2[1:0] = MemAddress[1:0]

  // Notes on the sheet:
  //   INPUTS to your circuit
  //   DON'T CHANGE THE LOCATIONS OF THE INPUTS AND OUTPUTS!
  //   OUTPUT from your circuit
endmodule
