// Logisim project regfile.circ as structural Verilog: 1 circuit, main circuit regfile
module regfile (
  input  [4:0] ReadIndex1,
  input  [4:0] ReadIndex2,
  input  [4:0] WriteIndex,
  input  [31:0] WriteData,
  input  RegWEn,
  input  clk,
  output [31:0] ra,
  output [31:0] sp,
  output [31:0] t0,
  output [31:0] t1,
  output [31:0] t2,
  output [31:0] s0,
  output [31:0] s1,
  output [31:0] a0,
  output [31:0] ReadData1,
  output [31:0] ReadData2
);

  wire and_1_out, and_2_out, and_3_out, and_4_out, and_5_out, and_6_out, and_7_out, and_8_out, and_9_out,
       and_10_out, and_11_out, and_12_out, and_13_out, and_14_out, and_15_out, and_16_out, and_17_out,
       and_18_out, and_19_out, and_20_out, and_21_out, and_22_out, and_23_out, and_24_out, and_25_out,
       and_26_out, and_27_out, and_28_out, and_29_out, and_30_out, and_31_out, and_32_out, decoder_1_out0,
       decoder_1_out1, decoder_1_out2, decoder_1_out3, decoder_1_out4, decoder_1_out5, decoder_1_out6,
       decoder_1_out7, decoder_1_out8, decoder_1_out9, decoder_1_out10, decoder_1_out11, decoder_1_out12,
       decoder_1_out13, decoder_1_out14, decoder_1_out15, decoder_1_out16, decoder_1_out17, decoder_1_out18,
       decoder_1_out19, decoder_1_out20, decoder_1_out21, decoder_1_out22, decoder_1_out23, decoder_1_out24,
       decoder_1_out25, decoder_1_out26, decoder_1_out27, decoder_1_out28, decoder_1_out29, decoder_1_out30,
       decoder_1_out31;
  wire [31:0] x0_q, x3_q, x4_q, x11_q, x12_q, x13_q, x14_q, x15_q, x16_q, x17_q, x18_q, x19_q, x20_q, x21_q,
       x22_q, x23_q, x24_q, x25_q, x26_q, x27_q, x28_q, x29_q, x30_q, x31_q;

  Decoder #(.select(5)) decoder_1 (
    .out0(decoder_1_out0), .out1(decoder_1_out1), .out2(decoder_1_out2), .out3(decoder_1_out3),
    .out4(decoder_1_out4), .out5(decoder_1_out5), .out6(decoder_1_out6), .out7(decoder_1_out7),
    .out8(decoder_1_out8), .out9(decoder_1_out9), .out10(decoder_1_out10), .out11(decoder_1_out11),
    .out12(decoder_1_out12), .out13(decoder_1_out13), .out14(decoder_1_out14), .out15(decoder_1_out15),
    .out16(decoder_1_out16), .out17(decoder_1_out17), .out18(decoder_1_out18), .out19(decoder_1_out19),
    .out20(decoder_1_out20), .out21(decoder_1_out21), .out22(decoder_1_out22), .out23(decoder_1_out23),
    .out24(decoder_1_out24), .out25(decoder_1_out25), .out26(decoder_1_out26), .out27(decoder_1_out27),
    .out28(decoder_1_out28), .out29(decoder_1_out29), .out30(decoder_1_out30), .out31(decoder_1_out31),
    .sel(WriteIndex));  // open: en
  and and_1 (and_1_out, decoder_1_out0, RegWEn);
  and and_2 (and_2_out, decoder_1_out1, RegWEn);
  and and_3 (and_3_out, decoder_1_out2, RegWEn);
  and and_4 (and_4_out, decoder_1_out3, RegWEn);
  and and_5 (and_5_out, decoder_1_out4, RegWEn);
  and and_6 (and_6_out, decoder_1_out5, RegWEn);
  and and_7 (and_7_out, decoder_1_out6, RegWEn);
  and and_8 (and_8_out, decoder_1_out7, RegWEn);
  and and_9 (and_9_out, decoder_1_out8, RegWEn);
  and and_10 (and_10_out, decoder_1_out9, RegWEn);
  and and_11 (and_11_out, decoder_1_out10, RegWEn);
  and and_12 (and_12_out, decoder_1_out11, RegWEn);
  and and_13 (and_13_out, decoder_1_out12, RegWEn);
  and and_14 (and_14_out, decoder_1_out13, RegWEn);
  and and_15 (and_15_out, decoder_1_out14, RegWEn);
  and and_16 (and_16_out, decoder_1_out15, RegWEn);
  and and_17 (and_17_out, decoder_1_out16, RegWEn);
  and and_18 (and_18_out, decoder_1_out17, RegWEn);
  and and_19 (and_19_out, decoder_1_out18, RegWEn);
  and and_20 (and_20_out, decoder_1_out19, RegWEn);
  and and_21 (and_21_out, decoder_1_out20, RegWEn);
  and and_22 (and_22_out, decoder_1_out21, RegWEn);
  and and_23 (and_23_out, decoder_1_out22, RegWEn);
  and and_24 (and_24_out, decoder_1_out23, RegWEn);
  and and_25 (and_25_out, decoder_1_out24, RegWEn);
  and and_26 (and_26_out, decoder_1_out25, RegWEn);
  and and_27 (and_27_out, decoder_1_out26, RegWEn);
  and and_28 (and_28_out, decoder_1_out27, RegWEn);
  and and_29 (and_29_out, decoder_1_out28, RegWEn);
  and and_30 (and_30_out, decoder_1_out29, RegWEn);
  and and_31 (and_31_out, decoder_1_out30, RegWEn);
  and and_32 (and_32_out, decoder_1_out31, RegWEn);
  Register #(.width(32)) x0 (.D({32{1'b0}}), .en(and_1_out), .clk(clk), .Q(x0_q));  // open: clr
  Register #(.width(32)) x1 (.D(WriteData), .en(and_2_out), .clk(clk), .Q(ra));  // open: clr
  Register #(.width(32)) x2 (.D(WriteData), .en(and_3_out), .clk(clk), .Q(sp));  // open: clr
  Register #(.width(32)) x3 (.D(WriteData), .en(and_4_out), .clk(clk), .Q(x3_q));  // open: clr
  Register #(.width(32)) x4 (.D(WriteData), .en(and_5_out), .clk(clk), .Q(x4_q));  // open: clr
  Register #(.width(32)) x5 (.D(WriteData), .en(and_6_out), .clk(clk), .Q(t0));  // open: clr
  Register #(.width(32)) x6 (.D(WriteData), .en(and_7_out), .clk(clk), .Q(t1));  // open: clr
  Register #(.width(32)) x7 (.D(WriteData), .en(and_8_out), .clk(clk), .Q(t2));  // open: clr
  Register #(.width(32)) x8 (.D(WriteData), .en(and_9_out), .clk(clk), .Q(s0));  // open: clr
  Register #(.width(32)) x9 (.D(WriteData), .en(and_10_out), .clk(clk), .Q(s1));  // open: clr
  Register #(.width(32)) x10 (.D(WriteData), .en(and_11_out), .clk(clk), .Q(a0));  // open: clr
  Register #(.width(32)) x11 (.D(WriteData), .en(and_12_out), .clk(clk), .Q(x11_q));  // open: clr
  Register #(.width(32)) x12 (.D(WriteData), .en(and_13_out), .clk(clk), .Q(x12_q));  // open: clr
  Register #(.width(32)) x13 (.D(WriteData), .en(and_14_out), .clk(clk), .Q(x13_q));  // open: clr
  Register #(.width(32)) x14 (.D(WriteData), .en(and_15_out), .clk(clk), .Q(x14_q));  // open: clr
  Register #(.width(32)) x15 (.D(WriteData), .en(and_16_out), .clk(clk), .Q(x15_q));  // open: clr
  Register #(.width(32)) x16 (.D(WriteData), .en(and_17_out), .clk(clk), .Q(x16_q));  // open: clr
  Register #(.width(32)) x17 (.D(WriteData), .en(and_18_out), .clk(clk), .Q(x17_q));  // open: clr
  Register #(.width(32)) x18 (.D(WriteData), .en(and_19_out), .clk(clk), .Q(x18_q));  // open: clr
  Register #(.width(32)) x19 (.D(WriteData), .en(and_20_out), .clk(clk), .Q(x19_q));  // open: clr
  Register #(.width(32)) x20 (.D(WriteData), .en(and_21_out), .clk(clk), .Q(x20_q));  // open: clr
  Register #(.width(32)) x21 (.D(WriteData), .en(and_22_out), .clk(clk), .Q(x21_q));  // open: clr
  Register #(.width(32)) x22 (.D(WriteData), .en(and_23_out), .clk(clk), .Q(x22_q));  // open: clr
  Register #(.width(32)) x23 (.D(WriteData), .en(and_24_out), .clk(clk), .Q(x23_q));  // open: clr
  Register #(.width(32)) x24 (.D(WriteData), .en(and_25_out), .clk(clk), .Q(x24_q));  // open: clr
  Register #(.width(32)) x25 (.D(WriteData), .en(and_26_out), .clk(clk), .Q(x25_q));  // open: clr
  Register #(.width(32)) x26 (.D(WriteData), .en(and_27_out), .clk(clk), .Q(x26_q));  // open: clr
  Register #(.width(32)) x27 (.D(WriteData), .en(and_28_out), .clk(clk), .Q(x27_q));  // open: clr
  Register #(.width(32)) x28 (.D(WriteData), .en(and_29_out), .clk(clk), .Q(x28_q));  // open: clr
  Register #(.width(32)) x29 (.D(WriteData), .en(and_30_out), .clk(clk), .Q(x29_q));  // open: clr
  Register #(.width(32)) x30 (.D(WriteData), .en(and_31_out), .clk(clk), .Q(x30_q));  // open: clr
  Register #(.width(32)) x31 (.D(WriteData), .en(and_32_out), .clk(clk), .Q(x31_q));  // open: clr
  Multiplexer #(.select(5), .width(32)) multiplexer_1 (
    .in0(x0_q), .in1(ra), .in2(sp), .in3(x3_q), .in4(x4_q), .in5(t0), .in6(t1), .in7(t2), .in8(s0), .in9(s1),
    .in10(a0), .in11(x11_q), .in12(x12_q), .in13(x13_q), .in14(x14_q), .in15(x15_q), .in16(x16_q),
    .in17(x17_q), .in18(x18_q), .in19(x19_q), .in20(x20_q), .in21(x21_q), .in22(x22_q), .in23(x23_q),
    .in24(x24_q), .in25(x25_q), .in26(x26_q), .in27(x27_q), .in28(x28_q), .in29(x29_q), .in30(x30_q),
    .in31(x31_q), .out(ReadData1), .sel(ReadIndex1));
  Multiplexer #(.select(5), .width(32)) multiplexer_2 (
    .in0(x0_q), .in1(ra), .in2(sp), .in3(x3_q), .in4(x4_q), .in5(t0), .in6(t1), .in7(t2), .in8(s0), .in9(s1),
    .in10(a0), .in11(x11_q), .in12(x12_q), .in13(x13_q), .in14(x14_q), .in15(x15_q), .in16(x16_q),
    .in17(x17_q), .in18(x18_q), .in19(x19_q), .in20(x20_q), .in21(x21_q), .in22(x22_q), .in23(x23_q),
    .in24(x24_q), .in25(x25_q), .in26(x26_q), .in27(x27_q), .in28(x28_q), .in29(x29_q), .in30(x30_q),
    .in31(x31_q), .out(ReadData2), .sel(ReadIndex2));

  // Notes on the sheet:
  //   INPUTS to your circuit
  //   DON'T CHANGE THE LOCATIONS OF THE INPUTS AND OUTPUTS!
  //   These are DEBUG/TEST outputs from your circuit.
  //   OUTPUTS from your circuit
endmodule
